// Logisim project IT012_Lab01_25520694.circ as structural Verilog: 5 circuits, main circuit TN1
module TN1 (
  input  A,
  input  B,
  input  C,
  output NOT,
  output AND,
  output OR,
  output NAND,
  output NOR,
  output XOR,
  output NXOR,
  output XOR3,
  output NAND3,
  output CHAIN
);

  wire nand_1_out;

  not not_1 (NOT, A);
  nand nand_1 (nand_1_out, A, B);
  and and_1 (AND, A, B);
  or or_1 (OR, A, B);
  nand nand_2 (NAND, A, B);
  nor nor_1 (NOR, A, B);
  xor xor_1 (XOR, A, B);
  xnor xnor_1 (NXOR, A, B);
  ExactlyOne xor_2 (.out(XOR3), .in0(A), .in1(B), .in2(C));
  nand nand_3 (NAND3, A, B, C);
  nand nand_4 (CHAIN, nand_1_out, C);
endmodule

module TN2 (
  input  x,
  input  y,
  input  z,
  output EQ1,
  output EQ2,
  output EQ4,
  output EQ5,
  output EQ3
);

  wire and_1_out, and_2_out, and_3_out, and_4_out, nand_1_out, not_1_out, not_2_out, not_3_out, not_4_out,
       or_1_out, or_2_out, or_3_out, or_4_out, or_5_out, or_6_out;

  not not_1 (not_1_out, x);
  not not_2 (not_2_out, x);
  not not_3 (not_3_out, y);
  and and_1 (and_1_out, not_2_out, not_3_out);
  or or_1 (or_1_out, x, y);
  not not_4 (not_4_out, or_1_out);
  nand nand_1 (nand_1_out, x, y);
  and and_2 (and_2_out, not_1_out, y);
  or or_2 (or_2_out, x, y);
  and and_3 (and_3_out, z, y);
  or or_3 (or_3_out, z, x);
  or or_4 (or_4_out, x, y);
  or or_5 (or_5_out, and_2_out, x);
  or or_6 (or_6_out, and_3_out, x);
  and and_4 (and_4_out, or_3_out, or_4_out);
  xnor xnor_1 (EQ1, and_1_out, not_4_out);
  xnor xnor_2 (EQ2, and_1_out, nand_1_out);
  xnor xnor_3 (EQ4, or_5_out, x);
  xnor xnor_4 (EQ5, or_5_out, or_2_out);
  xnor xnor_5 (EQ3, or_6_out, and_4_out);
endmodule

module TN3 (
  input  A,
  input  B,
  input  C,
  input  D,
  output F
);

  wire and_1_out, and_2_out, and_3_out, and_4_out, and_5_out, and_6_out, not_1_out, not_2_out, not_3_out,
       not_4_out;

  not not_1 (not_1_out, A);
  not not_2 (not_2_out, B);
  not not_3 (not_3_out, C);
  not not_4 (not_4_out, D);
  and and_1 (and_1_out, not_1_out, not_2_out, C, not_4_out);
  and and_2 (and_2_out, not_1_out, not_2_out, C, D);
  and and_3 (and_3_out, not_1_out, B, not_3_out, D);
  and and_4 (and_4_out, not_1_out, B, C, D);
  and and_5 (and_5_out, A, not_2_out, C, D);
  and and_6 (and_6_out, A, B, not_3_out, D);
  or or_1 (F, and_1_out, and_2_out, and_3_out, and_4_out, and_5_out, and_6_out);
endmodule

module TN4 (
  input  A,
  input  B,
  input  C,
  input  D,
  output F_can,
  output EQ1,
  output F_sop,
  output EQ2,
  output F_pos
);

  wire and_1_out, and_2_out, and_3_out, and_4_out, and_5_out, and_6_out, and_7_out, and_8_out, and_9_out,
       and_10_out, not_1_out, not_2_out, not_3_out, not_4_out, or_1_out, or_2_out, or_3_out, or_4_out;

  not not_1 (not_1_out, A);
  not not_2 (not_2_out, B);
  not not_3 (not_3_out, C);
  not not_4 (not_4_out, D);
  and and_1 (and_1_out, not_1_out, not_2_out, C, not_4_out);
  and and_2 (and_2_out, not_1_out, not_2_out, C, D);
  and and_3 (and_3_out, not_1_out, B, not_3_out, D);
  and and_4 (and_4_out, not_1_out, B, C, D);
  and and_5 (and_5_out, A, not_2_out, C, D);
  and and_6 (and_6_out, A, B, not_3_out, D);
  and and_7 (and_7_out, not_1_out, not_2_out, C);
  and and_8 (and_8_out, not_1_out, B, D);
  and and_9 (and_9_out, B, not_3_out, D);
  and and_10 (and_10_out, not_2_out, C, D);
  or or_1 (or_1_out, B, C);
  or or_2 (or_2_out, not_2_out, D);
  or or_3 (or_3_out, not_1_out, D);
  or or_4 (or_4_out, not_1_out, not_2_out, not_3_out);
  or or_5 (F_can, and_1_out, and_2_out, and_3_out, and_4_out, and_5_out, and_6_out);
  or or_6 (F_sop, and_7_out, and_8_out, and_9_out, and_10_out);
  and and_11 (F_pos, or_1_out, or_2_out, or_3_out, or_4_out);
  xnor xnor_1 (EQ1, F_can, F_sop);
  xnor xnor_2 (EQ2, F_can, F_pos);
endmodule

module TN5 (
  input  A,
  input  B,
  input  C,
  output F
);

  wire xor_1_out;

  xor xor_1 (xor_1_out, B, A);
  xor xor_2 (F, C, xor_1_out);
endmodule
