// Logisim project lab2.circ as structural Verilog: 8 circuits, main circuit FA
module FA (
  input  A,
  input  B,
  input  Cin,
  output S,
  output Cout
);

  wire and_1_out, and_2_out, xor_1_out;

  xor xor_1 (xor_1_out, A, B);
  and and_1 (and_1_out, A, B);
  and and_2 (and_2_out, xor_1_out, Cin);
  or or_1 (Cout, and_1_out, and_2_out);
  xor xor_2 (S, xor_1_out, Cin);
endmodule

module ADDSUB4 (
  input  [3:0] A,
  input  SUB,
  input  [3:0] B,
  output [3:0] S
);

  wire fa_1_cout, fa_2_cout, fa_3_cout, fa_4_cout, xor_1_out, xor_2_out, xor_3_out, xor_4_out;

  xor xor_1 (xor_1_out, SUB, B[0]);
  xor xor_2 (xor_2_out, SUB, B[1]);
  xor xor_3 (xor_3_out, SUB, B[2]);
  FA fa_1 (.A(A[0]), .B(xor_1_out), .Cin(SUB), .S(S[0]), .Cout(fa_1_cout));
  FA fa_2 (.A(A[1]), .B(xor_2_out), .Cin(fa_1_cout), .S(S[1]), .Cout(fa_2_cout));
  FA fa_3 (.A(A[2]), .B(xor_3_out), .Cin(fa_2_cout), .S(S[2]), .Cout(fa_3_cout));
  FA fa_4 (.A(A[3]), .B(xor_4_out), .Cin(fa_3_cout), .S(S[3]), .Cout(fa_4_cout));
  xor xor_4 (xor_4_out, SUB, B[3]);
  // Probe on fa_1_cout
  // Probe on fa_2_cout
  // Probe on fa_3_cout
  // Probe on fa_4_cout
endmodule

module ALU8 (
  input  [7:0] A,
  input  [7:0] B,
  input  [2:0] OP,
  output LT,
  output [7:0] R,
  output Z
);

  wire adder_1_cout, adder_2_cout, subtractor_1_bout;
  wire [7:0] adder_1_out, adder_2_out, and_1_out, multiplexer_1_out, multiplexer_2_out, not_1_out, or_1_out,
       subtractor_1_out, subtractor_2_out, xor_1_out;

  Adder adder_1 (.a(A), .b(B), .out(adder_1_out), .cout(adder_1_cout));  // open: cin
  Adder adder_2 (.a(A), .b(8'h1), .out(adder_2_out), .cin(adder_1_cout), .cout(adder_2_cout));
  Subtractor subtractor_1 (.a(A), .b(B), .out(subtractor_1_out), .bin(adder_2_cout), .bout(subtractor_1_bout));
  Subtractor subtractor_2 (.a(A), .b(8'h1), .out(subtractor_2_out), .bin(subtractor_1_bout));  // open: bout
  assign and_1_out = A & B;  // AND_Gate and_1, 8 bits wide
  assign or_1_out = A | B;  // OR_Gate or_1, 8 bits wide
  assign not_1_out = ~A;  // NOT_Gate not_1, 8 bits wide
  assign xor_1_out = A ^ B;  // XOR_Gate xor_1, 8 bits wide
  Multiplexer #(.select(2), .width(8)) multiplexer_1 (
    .in0(adder_1_out), .in1(adder_2_out), .in2(subtractor_1_out), .in3(subtractor_2_out),
    .out(multiplexer_1_out), .sel(OP[1:0]));  // open: en
  Multiplexer #(.select(2), .width(8)) multiplexer_2 (
    .in0(and_1_out), .in1(or_1_out), .in2(not_1_out), .in3(xor_1_out), .out(multiplexer_2_out), .sel(OP[1:0]));  // open: en
  LT lt_1 (.A7(A[7]), .B7(B[7]), .R7(R[7]), .LT(LT));
  Multiplexer #(.width(8)) multiplexer_3 (
    .in0(multiplexer_1_out), .in1(multiplexer_2_out), .out(R), .sel(OP[2]));  // open: en
  nor nor_1 (Z, R[0], R[1], R[2], R[3], R[4], R[5], R[6], R[7]);
endmodule

module LT (
  input  A7,
  input  B7,
  input  R7,
  output LT
);

  wire and_1_out, and_2_out, and_3_out, not_1_out;

  not not_1 (not_1_out, B7);
  and and_1 (and_1_out, A7, not_1_out);
  and and_2 (and_2_out, not_1_out, R7);
  and and_3 (and_3_out, A7, R7);
  or or_1 (LT, and_1_out, and_2_out, and_3_out);
endmodule

module DLATCH (
  input  D,
  input  E,
  output Q
);

  Multiplexer multiplexer_1 (.in0(Q), .in1(D), .out(Q), .sel(E));  // open: en
endmodule

module TN3 (
  input  D,
  input  E,
  output Q1,
  output Q2,
  output out_5,
  output out_6
);

  wire CLK_out, d_ff_1_q, dlatch_1_q;

  Clock CLK (.out(CLK_out));
  DLATCH dlatch_1 (.D(D), .E(CLK_out), .Q(dlatch_1_q));
  D_Flip_Flop d_ff_1 (.clk(CLK_out), .D(D), .Q(d_ff_1_q));  // open: Qn, preset, en, reset
  DLATCH dlatch_2 (.D(D), .E(E), .Q(Q1));
  D_Flip_Flop d_ff_2 (.clk(CLK_out), .D(D), .Q(Q2));  // open: Qn, preset, en, reset
  DLATCH dlatch_3 (.D(dlatch_1_q), .E(CLK_out), .Q(out_5));
  D_Flip_Flop d_ff_3 (.clk(CLK_out), .D(d_ff_1_q), .Q(out_6));  // open: Qn, preset, en, reset
endmodule

module REGFILE (
  input  [7:0] DIN,
  input  WE,
  input  [1:0] RA,
  input  [1:0] RD,
  input  [1:0] RB,
  output [7:0] QA,
  output [7:0] QB
);

  wire CLK_out, decoder_1_out0, decoder_1_out1, decoder_1_out2, decoder_1_out3;
  wire [7:0] R0_q, R1_q, R2_q, R3_q;

  Decoder #(.select(2)) decoder_1 (
    .out0(decoder_1_out0), .out1(decoder_1_out1), .out2(decoder_1_out2), .out3(decoder_1_out3), .sel(RD),
    .en(WE));
  Clock CLK (.out(CLK_out));
  Register R0 (.D(DIN), .en(decoder_1_out0), .Q(R0_q), .clk(CLK_out));  // open: clr
  Register R1 (.D(DIN), .en(decoder_1_out1), .Q(R1_q), .clk(CLK_out));  // open: clr
  Register R2 (.D(DIN), .en(decoder_1_out2), .Q(R2_q), .clk(CLK_out));  // open: clr
  Register R3 (.D(DIN), .en(decoder_1_out3), .Q(R3_q), .clk(CLK_out));  // open: clr
  Multiplexer #(.select(2), .width(8)) multiplexer_1 (
    .in0(R0_q), .in1(R1_q), .in2(R2_q), .in3(R3_q), .out(QA), .sel(RA));  // open: en
  Multiplexer #(.select(2), .width(8)) multiplexer_2 (
    .in0(R0_q), .in1(R1_q), .in2(R2_q), .in3(R3_q), .out(QB), .sel(RB));  // open: en
endmodule

module DATAPATH (
  input  [7:0] IMM,
  input  [2:0] OP,
  input  SRC,
  input  [1:0] RA,
  input  [1:0] RD,
  input  [1:0] RB,
  input  WE,
  output Z
);

  wire CLK_out;
  wire [7:0] alu8_1_r, multiplexer_1_out, regfile_1_qa, regfile_1_qb;

  ALU8 alu8_1 (.OP(OP), .A(regfile_1_qa), .B(regfile_1_qb), .R(alu8_1_r), .Z(Z));  // open: LT
  Clock CLK (.out(CLK_out));
  Multiplexer #(.width(8)) multiplexer_1 (.in0(alu8_1_r), .in1(IMM), .out(multiplexer_1_out), .sel(SRC));  // open: en
  REGFILE regfile_1 (.DIN(multiplexer_1_out), .RA(RA), .RD(RD), .RB(RB), .WE(WE), .QA(regfile_1_qa), .QB(regfile_1_qb));
endmodule
